# Fritzing sketch esp32_complete_circuit (saved by Fritzing 0.9.3b)
breadboards: 1

parts:
  U1 = LuaNode32 / ESP32
  RHT1 = Humidity and Temperature Sensor RHT03
  R1 = Resistor [tolerance=±5% resistance=33 package=THT]  # not connected
  R2 = Resistor [tolerance=±5% resistance=10k package=THT]
  SD_card_module1 = SD Card Module
  C1 = Electrolytic Capacitor [capacitance=10µF package="100 mil [THT, electrolytic]"]  # not connected

nets:
  3V3: U1.3V3, RHT1.Vcc, R2.Pin_0, SD_card_module1.+3.3
  N1: U1.GND, RHT1.GND_2, SD_card_module1.GND#0
  N2: U1.D4, RHT1.Data-signal, R2.Pin_1
  N3: U1.D5, SD_card_module1.CS
  N4: U1.D18, SD_card_module1.SCK
  N5: U1.D19, SD_card_module1.MISO
  N6: U1.D23, SD_card_module1.MOSI

custom parts:
  LuaNode32 / ESP32: ESP32 based LuaNode32
  SD Card Module: SD Card Module Slot Socket Reader For Arduino ARM MCU
